# Fritzing sketch Schematic (saved by Fritzing 0.9.3b)
breadboards: 1

parts:
  Nano1 = Arduino Nano v2.3
  DFRobot_DFPlayer_Mini1 = DFRobot DFPlayer Mini [part_number=DFR0299]
  Bauteil1 = RFID-RC522-v2
  SP1 = SPEAKER [package=pcb_mount_speaker]
  R1 = Resistor [tolerance=±5% resistance=1k package=THT]
  R2 = Resistor [tolerance=±5% resistance=1k package=THT]
  C1_100µF = Capacitor Polarized [package=cpol-radial-100uf-25v]
  C2_100nF = Ceramic Capacitor [capacitance=100nF package="100 mil [THT, multilayer]"]
  S1_Play/Pause = Pushbutton [package=THT]
  S2_Next/Vol+ = Pushbutton [package=THT]
  S3_Prev/Vol- = Pushbutton [package=THT]
  Q1 = TRANSISTOR_NPN [part_number=IRLZ34N package=to-92-ammo]
  R3 = Resistor [tolerance=±5% resistance=1k package=THT]
  R4 = Resistor [tolerance=±5% resistance=25 package=THT]
  Power_Plug_5V = Power plug
  S2_Power_Switch = Toggle Switch [package=THT]
  Power_Bank_5V = 4 x AAA Battery Mount

nets:
  N1: Nano1.D2, R2.Pin_0
  N2: Nano1.D3, R1.Pin_0
  N3: Nano1.D4, DFRobot_DFPlayer_Mini1.BUSY
  N4: Nano1.D8, R3.Pin_1
  N5: Nano1.D9, Bauteil1.GND
  N6: Nano1.D10, Bauteil1.SDA
  N7: Nano1.D11, Bauteil1.MOSI
  N8: Nano1.D12, Bauteil1.MISO
  N9: Nano1.D13, Bauteil1.SCK
  3V3: Nano1.3V3, Bauteil1.3.3V
  N10: Nano1.A2, S3_Prev/Vol-.leg1
  N11: Nano1.A1, S2_Next/Vol+.leg1
  N12: Nano1.A0, S1_Play/Pause.leg1
  N13: Nano1.+5V, C1_100µF.+, C2_100nF.1, R4.Pin_1, S2_Power_Switch.L2
  GND: Nano1.GND, DFRobot_DFPlayer_Mini1.GND-1, DFRobot_DFPlayer_Mini1.GND-2
  N14: DFRobot_DFPlayer_Mini1.RX, R1.Pin_1
  N15: DFRobot_DFPlayer_Mini1.TX, R2.Pin_1
  N16: DFRobot_DFPlayer_Mini1.SPK_1, SP1.-
  N17: DFRobot_DFPlayer_Mini1.SPK_2, SP1.+
  N18: C1_100µF.-, C2_100nF.0, Power_Plug_5V.GND, Power_Bank_5V.-
  N19: S1_Play/Pause.leg0, S2_Next/Vol+.leg0
  N20: Q1.B, R3.Pin_0
  N21: Q1.C, R4.Pin_0
  N22: Power_Plug_5V.VCC, S2_Power_Switch.COM, Power_Bank_5V.+

notes:
  Control Buttons
  Buttons
  Voltage
  Power Bank
  keep alive
  Stabilization
  Ic 500mA - 200mA
  10 - 25Ω
  IRLZ34N

custom parts:
  RFID-RC522-v2: A simple China made RFID-RC522 Reader; do check the pin labels, as this is a MFRC522 based clone.
